// Digital circuit 16bit-full-adder.dig as structural Verilog
module _16bit_full_adder (
  input  [15:0] A,
  input  [15:0] B,
  output [15:0] Sum,
  output Carry
);

  wire _74283_1_pin9, _74283_2_pin9, _74283_3_pin9;

  _74283 _74283_1 (
    .pin1(Sum[1]), .pin2(B[1]), .pin3(A[1]), .pin4(Sum[0]), .pin5(A[0]), .pin6(B[0]), .pin7(1'b0),
    .pin8(1'b0), .pin9(_74283_1_pin9), .pin10(Sum[3]), .pin11(B[3]), .pin12(A[3]), .pin13(Sum[2]),
    .pin14(A[2]), .pin15(B[2]), .pin16(1'b1));
  _74283 _74283_2 (
    .pin1(Sum[5]), .pin2(B[5]), .pin3(A[5]), .pin4(Sum[4]), .pin5(A[4]), .pin6(B[4]), .pin7(_74283_1_pin9),
    .pin8(1'b0), .pin9(_74283_2_pin9), .pin10(Sum[7]), .pin11(B[7]), .pin12(A[7]), .pin13(Sum[6]),
    .pin14(A[6]), .pin15(B[6]), .pin16(1'b1));
  _74283 _74283_3 (
    .pin1(Sum[9]), .pin2(B[9]), .pin3(A[9]), .pin4(Sum[8]), .pin5(A[8]), .pin6(B[8]), .pin7(_74283_2_pin9),
    .pin8(1'b0), .pin9(_74283_3_pin9), .pin10(Sum[11]), .pin11(B[11]), .pin12(A[11]), .pin13(Sum[10]),
    .pin14(A[10]), .pin15(B[10]), .pin16(1'b1));
  _74283 _74283_4 (
    .pin1(Sum[13]), .pin2(B[13]), .pin3(A[13]), .pin4(Sum[12]), .pin5(A[12]), .pin6(B[12]),
    .pin7(_74283_3_pin9), .pin8(1'b0), .pin9(Carry), .pin10(Sum[15]), .pin11(B[15]), .pin12(A[15]),
    .pin13(Sum[14]), .pin14(A[14]), .pin15(B[14]), .pin16(1'b1));
endmodule

/* Test case:
A      B      Sum     
0      0      0 
0      65535  65535 
65535  65535  65534 
43690  21845  65535 
15555  4080   19635 
4660   39030  43690 
*/
