// Digital circuit 16bit-mux.dig as structural Verilog
module _16bit_mux (
  input  [15:0] A,
  input  S,
  input  [15:0] B,
  output [15:0] Out
);

  _74157 _74157_1 (
    .pin1(S), .pin2(A[0]), .pin3(B[0]), .pin4(Out[0]), .pin5(A[1]), .pin6(B[1]), .pin7(Out[1]), .pin8(1'b0),
    .pin9(Out[2]), .pin10(B[2]), .pin11(A[2]), .pin12(Out[3]), .pin13(B[3]), .pin14(A[3]), .pin15(1'b0),
    .pin16(1'b1));
  _74157 _74157_2 (
    .pin1(S), .pin2(A[4]), .pin3(B[4]), .pin4(Out[4]), .pin5(A[5]), .pin6(B[5]), .pin7(Out[5]), .pin8(1'b0),
    .pin9(Out[6]), .pin10(B[6]), .pin11(A[6]), .pin12(Out[7]), .pin13(B[7]), .pin14(A[7]), .pin15(1'b0),
    .pin16(1'b1));
  _74157 _74157_3 (
    .pin1(S), .pin2(A[8]), .pin3(B[8]), .pin4(Out[8]), .pin5(A[9]), .pin6(B[9]), .pin7(Out[9]), .pin8(1'b0),
    .pin9(Out[10]), .pin10(B[10]), .pin11(A[10]), .pin12(Out[11]), .pin13(B[11]), .pin14(A[11]),
    .pin15(1'b0), .pin16(1'b1));
  _74157 _74157_4 (
    .pin1(S), .pin2(A[12]), .pin3(B[12]), .pin4(Out[12]), .pin5(A[13]), .pin6(B[13]), .pin7(Out[13]),
    .pin8(1'b0), .pin9(Out[14]), .pin10(B[14]), .pin11(A[14]), .pin12(Out[15]), .pin13(B[15]), .pin14(A[15]),
    .pin15(1'b0), .pin16(1'b1));
endmodule
