// Digital circuit 16bit-program-counter.dig as structural Verilog
module _16bit_program_counter (
  input  EO,
  input  [15:0] D,
  input  Inc,
  input  Cl,
  input  Clr,
  input  Load,
  input  ED,
  output [15:0] Out
);

  wire _74161_1_pin11, _74161_1_pin12, _74161_1_pin13, _74161_1_pin14, _74161_1_pin15, _74161_2_pin11,
       _74161_2_pin12, _74161_2_pin13, _74161_2_pin14, _74161_2_pin15, _74161_3_pin11, _74161_3_pin12,
       _74161_3_pin13, _74161_3_pin14, _74161_3_pin15, _74161_4_pin11, _74161_4_pin12, _74161_4_pin13,
       _74161_4_pin14, _74245_3_pin11, _74245_3_pin12, _74245_3_pin13, _74245_3_pin14, _74245_3_pin15,
       _74245_3_pin16, _74245_3_pin17, _74245_3_pin18, _74245_4_pin11, _74245_4_pin12, _74245_4_pin13,
       _74245_4_pin14, _74245_4_pin15, _74245_4_pin16, _74245_4_pin17, _74245_4_pin18, not_1_out, not_2_out,
       not_3_out, not_4_out;

  not not_1 (not_1_out, Clr);
  not not_2 (not_2_out, Load);
  not not_3 (not_3_out, ED);
  not not_4 (not_4_out, EO);
  _74161 _74161_1 (
    .pin1(not_1_out), .pin2(Cl), .pin3(D[0]), .pin4(D[1]), .pin5(D[2]), .pin6(D[3]), .pin7(Inc), .pin8(1'b0),
    .pin9(not_2_out), .pin10(Inc), .pin11(_74161_1_pin11), .pin12(_74161_1_pin12), .pin13(_74161_1_pin13),
    .pin14(_74161_1_pin14), .pin15(_74161_1_pin15), .pin16(1'b1));
  _74161 _74161_2 (
    .pin1(not_1_out), .pin2(Cl), .pin3(D[4]), .pin4(D[5]), .pin5(D[6]), .pin6(D[7]), .pin7(Inc), .pin8(1'b0),
    .pin9(not_2_out), .pin10(_74161_1_pin15), .pin11(_74161_2_pin11), .pin12(_74161_2_pin12),
    .pin13(_74161_2_pin13), .pin14(_74161_2_pin14), .pin15(_74161_2_pin15), .pin16(1'b1));
  _74161 _74161_3 (
    .pin1(not_1_out), .pin2(Cl), .pin3(D[8]), .pin4(D[9]), .pin5(D[10]), .pin6(D[11]), .pin7(Inc),
    .pin8(1'b0), .pin9(not_2_out), .pin10(_74161_2_pin15), .pin11(_74161_3_pin11), .pin12(_74161_3_pin12),
    .pin13(_74161_3_pin13), .pin14(_74161_3_pin14), .pin15(_74161_3_pin15), .pin16(1'b1));
  _74161 _74161_4 (
    .pin1(not_1_out), .pin2(Cl), .pin3(D[12]), .pin4(D[13]), .pin5(D[14]), .pin6(D[15]), .pin7(Inc),
    .pin8(1'b0), .pin9(not_2_out), .pin10(_74161_3_pin15), .pin11(_74161_4_pin11), .pin12(_74161_4_pin12),
    .pin13(_74161_4_pin13), .pin14(_74161_4_pin14), .pin16(1'b1));  // open: pin15
  _74245 _74245_1 (
    .pin1(1'b1), .pin2(_74161_1_pin14), .pin3(_74161_1_pin13), .pin4(_74161_1_pin12), .pin5(_74161_1_pin11),
    .pin6(_74161_2_pin14), .pin7(_74161_2_pin13), .pin8(_74161_2_pin12), .pin9(_74161_2_pin11), .pin10(1'b0),
    .pin11(Out[7]), .pin12(Out[6]), .pin13(Out[5]), .pin14(Out[4]), .pin15(Out[3]), .pin16(Out[2]),
    .pin17(Out[1]), .pin18(Out[0]), .pin19(not_4_out), .pin20(1'b1));
  _74245 _74245_2 (
    .pin1(1'b1), .pin2(_74161_3_pin14), .pin3(_74161_3_pin13), .pin4(_74161_3_pin12), .pin5(_74161_3_pin11),
    .pin6(_74161_4_pin14), .pin7(_74161_4_pin13), .pin8(_74161_4_pin12), .pin9(_74161_4_pin11), .pin10(1'b0),
    .pin11(Out[15]), .pin12(Out[14]), .pin13(Out[13]), .pin14(Out[12]), .pin15(Out[11]), .pin16(Out[10]),
    .pin17(Out[9]), .pin18(Out[8]), .pin19(not_4_out), .pin20(1'b1));
  _74245 _74245_3 (
    .pin1(1'b1), .pin2(_74161_1_pin14), .pin3(_74161_1_pin13), .pin4(_74161_1_pin12), .pin5(_74161_1_pin11),
    .pin6(_74161_2_pin14), .pin7(_74161_2_pin13), .pin8(_74161_2_pin12), .pin9(_74161_2_pin11), .pin10(1'b0),
    .pin11(_74245_3_pin11), .pin12(_74245_3_pin12), .pin13(_74245_3_pin13), .pin14(_74245_3_pin14),
    .pin15(_74245_3_pin15), .pin16(_74245_3_pin16), .pin17(_74245_3_pin17), .pin18(_74245_3_pin18),
    .pin19(not_3_out), .pin20(1'b1));
  _74245 _74245_4 (
    .pin1(1'b1), .pin2(_74161_3_pin14), .pin3(_74161_3_pin13), .pin4(_74161_3_pin12), .pin5(_74161_3_pin11),
    .pin6(_74161_4_pin14), .pin7(_74161_4_pin13), .pin8(_74161_4_pin12), .pin9(_74161_4_pin11), .pin10(1'b0),
    .pin11(_74245_4_pin11), .pin12(_74245_4_pin12), .pin13(_74245_4_pin13), .pin14(_74245_4_pin14),
    .pin15(_74245_4_pin15), .pin16(_74245_4_pin16), .pin17(_74245_4_pin17), .pin18(_74245_4_pin18),
    .pin19(not_3_out), .pin20(1'b1));
  LED led_1 (.in(_74245_4_pin11));
  LED led_2 (.in(_74245_4_pin13));
  LED led_3 (.in(_74245_4_pin12));
  LED led_4 (.in(_74245_4_pin15));
  LED led_5 (.in(_74245_4_pin14));
  LED led_6 (.in(_74245_4_pin17));
  LED led_7 (.in(_74245_4_pin16));
  LED led_8 (.in(_74245_3_pin11));
  LED led_9 (.in(_74245_4_pin18));
  LED led_10 (.in(_74245_3_pin13));
  LED led_11 (.in(_74245_3_pin12));
  LED led_12 (.in(_74245_3_pin15));
  LED led_13 (.in(_74245_3_pin14));
  LED led_14 (.in(_74245_3_pin17));
  LED led_15 (.in(_74245_3_pin16));
  LED led_16 (.in(_74245_3_pin18));
endmodule
