// Digital circuit 32KB-16bit-ROM.dig as structural Verilog
module _32KB_16bit_ROM (
  input  [15:0] A,
  output [15:0] D
);

  // _28c256 _28c256_1: pin names not known; wires that end beside it: A[14], A[12], A[7], A[6], A[5], A[4], A[3], A[2], A[1], A[0], D[8], D[9], D[10], 1'b0, 1'b1, 1'b1, A[13], A[8], A[9], A[11], 1'b0, A[10], 1'b0, D[15]
  // _28c256 _28c256_2: pin names not known; wires that end beside it: A[14], A[12], A[7], A[6], A[5], A[4], A[3], A[2], A[1], A[0], D[0], D[1], D[2], 1'b0, 1'b1, 1'b1, A[13], A[8], A[9], A[11], 1'b0, A[10], 1'b0, D[7]
endmodule
