// Digital circuit ALU.dig as structural Verilog
module ALU (
  input  [15:0] X,
  input  ZX,
  input  NX,
  input  NO,
  input  [15:0] Y,
  input  ZY,
  input  NY,
  input  F,
  input  ED,
  output [15:0] OUT,
  output NG,
  output ZR
);

  wire _7408_1_pin3, _7408_1_pin6, _7408_1_pin8, _7408_1_pin11, _7408_2_pin3, _7408_2_pin6, _7408_2_pin8,
       _7408_2_pin11, _7408_3_pin3, _7408_3_pin6, _7408_3_pin8, _7408_3_pin11, _7408_4_pin3, _7408_4_pin6,
       _7408_4_pin8, _7408_4_pin11, _74157_1_pin4, _74157_1_pin7, _74157_1_pin9, _74157_1_pin12,
       _74157_2_pin4, _74157_2_pin7, _74157_2_pin9, _74157_2_pin12, _74157_3_pin4, _74157_3_pin7,
       _74157_3_pin9, _74157_3_pin12, _74157_4_pin4, _74157_4_pin7, _74157_4_pin9, _74157_4_pin12,
       _74157_5_pin4, _74157_5_pin7, _74157_5_pin9, _74157_5_pin12, _74157_6_pin4, _74157_6_pin7,
       _74157_6_pin9, _74157_6_pin12, _74157_7_pin4, _74157_7_pin7, _74157_7_pin9, _74157_7_pin12,
       _74157_8_pin4, _74157_8_pin7, _74157_8_pin9, _74157_8_pin12, _74157_9_pin4, _74157_9_pin7,
       _74157_9_pin9, _74157_9_pin12, _74157_10_pin4, _74157_10_pin7, _74157_10_pin9, _74157_10_pin12,
       _74157_11_pin4, _74157_11_pin7, _74157_11_pin9, _74157_11_pin12, _74157_12_pin4, _74157_12_pin7,
       _74157_12_pin9, _74157_12_pin12, _74245_1_pin17, _74245_1_pin18, _74245_2_pin11, _74245_2_pin12,
       _74245_2_pin13, _74245_2_pin14, _74245_2_pin15, _74245_2_pin16, _74245_2_pin17, _74245_2_pin18,
       _74245_3_pin11, _74245_3_pin12, _74245_3_pin13, _74245_3_pin14, _74245_3_pin15, _74245_3_pin16,
       _74245_3_pin17, _74245_3_pin18, _74688_1_pin19, _74688_2_pin19, not_1_out;
  wire [15:0] _16bit_full_adder_1_sum, _7486_1_pin6, _7486_5_pin6;

  not not_1 (not_1_out, ED);
  _74157 _74157_1 (
    .pin1(ZX), .pin2(X[0]), .pin3(1'b0), .pin4(_74157_1_pin4), .pin5(X[1]), .pin6(1'b0),
    .pin7(_74157_1_pin7), .pin8(1'b0), .pin9(_74157_1_pin9), .pin10(1'b0), .pin11(X[2]),
    .pin12(_74157_1_pin12), .pin13(1'b0), .pin14(X[3]), .pin15(1'b0), .pin16(1'b1));
  _74157 _74157_2 (
    .pin1(ZX), .pin2(X[4]), .pin3(1'b0), .pin4(_74157_2_pin4), .pin5(X[5]), .pin6(1'b0),
    .pin7(_74157_2_pin7), .pin8(1'b0), .pin9(_74157_2_pin9), .pin10(1'b0), .pin11(X[6]),
    .pin12(_74157_2_pin12), .pin13(1'b0), .pin14(X[7]), .pin15(1'b0), .pin16(1'b1));
  _74157 _74157_3 (
    .pin1(ZX), .pin2(X[8]), .pin3(1'b0), .pin4(_74157_3_pin4), .pin5(X[9]), .pin6(1'b0),
    .pin7(_74157_3_pin7), .pin8(1'b0), .pin9(_74157_3_pin9), .pin10(1'b0), .pin11(X[10]),
    .pin12(_74157_3_pin12), .pin13(1'b0), .pin14(X[11]), .pin15(1'b0), .pin16(1'b1));
  _74157 _74157_4 (
    .pin1(ZX), .pin2(X[12]), .pin3(1'b0), .pin4(_74157_4_pin4), .pin5(X[13]), .pin6(1'b0),
    .pin7(_74157_4_pin7), .pin8(1'b0), .pin9(_74157_4_pin9), .pin10(1'b0), .pin11(X[14]),
    .pin12(_74157_4_pin12), .pin13(1'b0), .pin14(X[15]), .pin15(1'b0), .pin16(1'b1));
  _74157 _74157_5 (
    .pin1(ZY), .pin2(Y[0]), .pin3(1'b0), .pin4(_74157_5_pin4), .pin5(Y[1]), .pin6(1'b0),
    .pin7(_74157_5_pin7), .pin8(1'b0), .pin9(_74157_5_pin9), .pin10(1'b0), .pin11(Y[2]),
    .pin12(_74157_5_pin12), .pin13(1'b0), .pin14(Y[3]), .pin15(1'b0), .pin16(1'b1));
  _74157 _74157_6 (
    .pin1(ZY), .pin2(Y[4]), .pin3(1'b0), .pin4(_74157_6_pin4), .pin5(Y[5]), .pin6(1'b0),
    .pin7(_74157_6_pin7), .pin8(1'b0), .pin9(_74157_6_pin9), .pin10(1'b0), .pin11(Y[6]),
    .pin12(_74157_6_pin12), .pin13(1'b0), .pin14(Y[7]), .pin15(1'b0), .pin16(1'b1));
  _74157 _74157_7 (
    .pin1(ZY), .pin2(Y[8]), .pin3(1'b0), .pin4(_74157_7_pin4), .pin5(Y[9]), .pin6(1'b0),
    .pin7(_74157_7_pin7), .pin8(1'b0), .pin9(_74157_7_pin9), .pin10(1'b0), .pin11(Y[10]),
    .pin12(_74157_7_pin12), .pin13(1'b0), .pin14(Y[11]), .pin15(1'b0), .pin16(1'b1));
  _74157 _74157_8 (
    .pin1(ZY), .pin2(Y[12]), .pin3(1'b0), .pin4(_74157_8_pin4), .pin5(Y[13]), .pin6(1'b0),
    .pin7(_74157_8_pin7), .pin8(1'b0), .pin9(_74157_8_pin9), .pin10(1'b0), .pin11(Y[14]),
    .pin12(_74157_8_pin12), .pin13(1'b0), .pin14(Y[15]), .pin15(1'b0), .pin16(1'b1));
  _7486 _7486_1 (
    .pin1(_74157_1_pin4), .pin2(NX), .pin3(_7486_1_pin6[0]), .pin4(_74157_1_pin7), .pin5(NX),
    .pin6(_7486_1_pin6[1]), .pin7(1'b0), .pin8(_7486_1_pin6[2]), .pin9(_74157_1_pin9), .pin10(NX),
    .pin11(_7486_1_pin6[3]), .pin12(_74157_1_pin12), .pin13(NX), .pin14(1'b1));
  _7486 _7486_2 (
    .pin1(_74157_2_pin4), .pin2(NX), .pin3(_7486_1_pin6[4]), .pin4(_74157_2_pin7), .pin5(NX),
    .pin6(_7486_1_pin6[5]), .pin7(1'b0), .pin8(_7486_1_pin6[6]), .pin9(_74157_2_pin9), .pin10(NX),
    .pin11(_7486_1_pin6[7]), .pin12(_74157_2_pin12), .pin13(NX), .pin14(1'b1));
  _7486 _7486_3 (
    .pin1(_74157_3_pin4), .pin2(NX), .pin3(_7486_1_pin6[8]), .pin4(_74157_3_pin7), .pin5(NX),
    .pin6(_7486_1_pin6[9]), .pin7(1'b0), .pin8(_7486_1_pin6[10]), .pin9(_74157_3_pin9), .pin10(NX),
    .pin11(_7486_1_pin6[11]), .pin12(_74157_3_pin12), .pin13(NX), .pin14(1'b1));
  _7486 _7486_4 (
    .pin1(_74157_4_pin4), .pin2(NX), .pin3(_7486_1_pin6[12]), .pin4(_74157_4_pin7), .pin5(NX),
    .pin6(_7486_1_pin6[13]), .pin7(1'b0), .pin8(_7486_1_pin6[14]), .pin9(_74157_4_pin9), .pin10(NX),
    .pin11(_7486_1_pin6[15]), .pin12(_74157_4_pin12), .pin13(NX), .pin14(1'b1));
  _7486 _7486_5 (
    .pin1(_74157_5_pin4), .pin2(NY), .pin3(_7486_5_pin6[0]), .pin4(_74157_5_pin7), .pin5(NY),
    .pin6(_7486_5_pin6[1]), .pin7(1'b0), .pin8(_7486_5_pin6[2]), .pin9(_74157_5_pin9), .pin10(NY),
    .pin11(_7486_5_pin6[3]), .pin12(_74157_5_pin12), .pin13(NY), .pin14(1'b1));
  _7486 _7486_6 (
    .pin1(_74157_6_pin4), .pin2(NY), .pin3(_7486_5_pin6[4]), .pin4(_74157_6_pin7), .pin5(NY),
    .pin6(_7486_5_pin6[5]), .pin7(1'b0), .pin8(_7486_5_pin6[6]), .pin9(_74157_6_pin9), .pin10(NY),
    .pin11(_7486_5_pin6[7]), .pin12(_74157_6_pin12), .pin13(NY), .pin14(1'b1));
  _7486 _7486_7 (
    .pin1(_74157_7_pin4), .pin2(NY), .pin3(_7486_5_pin6[8]), .pin4(_74157_7_pin7), .pin5(NY),
    .pin6(_7486_5_pin6[9]), .pin7(1'b0), .pin8(_7486_5_pin6[10]), .pin9(_74157_7_pin9), .pin10(NY),
    .pin11(_7486_5_pin6[11]), .pin12(_74157_7_pin12), .pin13(NY), .pin14(1'b1));
  _7486 _7486_8 (
    .pin1(_74157_8_pin4), .pin2(NY), .pin3(_7486_5_pin6[12]), .pin4(_74157_8_pin7), .pin5(NY),
    .pin6(_7486_5_pin6[13]), .pin7(1'b0), .pin8(_7486_5_pin6[14]), .pin9(_74157_8_pin9), .pin10(NY),
    .pin11(_7486_5_pin6[15]), .pin12(_74157_8_pin12), .pin13(NY), .pin14(1'b1));
  _16bit_full_adder _16bit_full_adder_1 (
    .A(_7486_1_pin6), .B(_7486_5_pin6), .Sum(_16bit_full_adder_1_sum));  // open: Carry
  _7408 _7408_1 (
    .pin1(_7486_1_pin6[0]), .pin2(_7486_5_pin6[0]), .pin3(_7408_1_pin3), .pin4(_7486_1_pin6[1]),
    .pin5(_7486_5_pin6[1]), .pin6(_7408_1_pin6), .pin7(1'b0), .pin8(_7408_1_pin8), .pin9(_7486_1_pin6[2]),
    .pin10(_7486_5_pin6[2]), .pin11(_7408_1_pin11), .pin12(_7486_1_pin6[3]), .pin13(_7486_5_pin6[3]),
    .pin14(1'b1));
  _7408 _7408_2 (
    .pin1(_7486_1_pin6[4]), .pin2(_7486_5_pin6[4]), .pin3(_7408_2_pin3), .pin4(_7486_1_pin6[5]),
    .pin5(_7486_5_pin6[5]), .pin6(_7408_2_pin6), .pin7(1'b0), .pin8(_7408_2_pin8), .pin9(_7486_1_pin6[6]),
    .pin10(_7486_5_pin6[6]), .pin11(_7408_2_pin11), .pin12(_7486_1_pin6[7]), .pin13(_7486_5_pin6[7]),
    .pin14(1'b1));
  _7408 _7408_3 (
    .pin1(_7486_1_pin6[8]), .pin2(_7486_5_pin6[8]), .pin3(_7408_3_pin3), .pin4(_7486_1_pin6[9]),
    .pin5(_7486_5_pin6[9]), .pin6(_7408_3_pin6), .pin7(1'b0), .pin8(_7408_3_pin8), .pin9(_7486_1_pin6[10]),
    .pin10(_7486_5_pin6[10]), .pin11(_7408_3_pin11), .pin12(_7486_1_pin6[11]), .pin13(_7486_5_pin6[11]),
    .pin14(1'b1));
  _7408 _7408_4 (
    .pin1(_7486_1_pin6[12]), .pin2(_7486_5_pin6[12]), .pin3(_7408_4_pin3), .pin4(_7486_1_pin6[13]),
    .pin5(_7486_5_pin6[13]), .pin6(_7408_4_pin6), .pin7(1'b0), .pin8(_7408_4_pin8), .pin9(_7486_1_pin6[14]),
    .pin10(_7486_5_pin6[14]), .pin11(_7408_4_pin11), .pin12(_7486_1_pin6[15]), .pin13(_7486_5_pin6[15]),
    .pin14(1'b1));
  _74157 _74157_9 (
    .pin1(F), .pin2(_7408_1_pin3), .pin3(_16bit_full_adder_1_sum[0]), .pin4(_74157_9_pin4),
    .pin5(_7408_1_pin6), .pin6(_16bit_full_adder_1_sum[1]), .pin7(_74157_9_pin7), .pin8(1'b0),
    .pin9(_74157_9_pin9), .pin10(_16bit_full_adder_1_sum[2]), .pin11(_7408_1_pin8), .pin12(_74157_9_pin12),
    .pin13(_16bit_full_adder_1_sum[3]), .pin14(_7408_1_pin11), .pin15(1'b0), .pin16(1'b1));
  _74157 _74157_10 (
    .pin1(F), .pin2(_7408_2_pin3), .pin3(_16bit_full_adder_1_sum[4]), .pin4(_74157_10_pin4),
    .pin5(_7408_2_pin6), .pin6(_16bit_full_adder_1_sum[5]), .pin7(_74157_10_pin7), .pin8(1'b0),
    .pin9(_74157_10_pin9), .pin10(_16bit_full_adder_1_sum[6]), .pin11(_7408_2_pin8), .pin12(_74157_10_pin12),
    .pin13(_16bit_full_adder_1_sum[7]), .pin14(_7408_2_pin11), .pin15(1'b0), .pin16(1'b1));
  _74157 _74157_11 (
    .pin1(F), .pin2(_7408_3_pin3), .pin3(_16bit_full_adder_1_sum[8]), .pin4(_74157_11_pin4),
    .pin5(_7408_3_pin6), .pin6(_16bit_full_adder_1_sum[9]), .pin7(_74157_11_pin7), .pin8(1'b0),
    .pin9(_74157_11_pin9), .pin10(_16bit_full_adder_1_sum[10]), .pin11(_7408_3_pin8),
    .pin12(_74157_11_pin12), .pin13(_16bit_full_adder_1_sum[11]), .pin14(_7408_3_pin11), .pin15(1'b0),
    .pin16(1'b1));
  _74157 _74157_12 (
    .pin1(F), .pin2(_7408_4_pin3), .pin3(_16bit_full_adder_1_sum[12]), .pin4(_74157_12_pin4),
    .pin5(_7408_4_pin6), .pin6(_16bit_full_adder_1_sum[13]), .pin7(_74157_12_pin7), .pin8(1'b0),
    .pin9(_74157_12_pin9), .pin10(_16bit_full_adder_1_sum[14]), .pin11(_7408_4_pin8),
    .pin12(_74157_12_pin12), .pin13(_16bit_full_adder_1_sum[15]), .pin14(_7408_4_pin11), .pin15(1'b0),
    .pin16(1'b1));
  _7486 _7486_9 (
    .pin1(_74157_9_pin4), .pin2(NO), .pin3(OUT[0]), .pin4(_74157_9_pin7), .pin5(NO), .pin6(OUT[1]),
    .pin7(1'b0), .pin8(OUT[2]), .pin9(_74157_9_pin9), .pin10(NO), .pin11(OUT[3]), .pin12(_74157_9_pin12),
    .pin13(NO), .pin14(1'b1));
  _7486 _7486_10 (
    .pin1(_74157_10_pin4), .pin2(NO), .pin3(OUT[4]), .pin4(_74157_10_pin7), .pin5(NO), .pin6(OUT[5]),
    .pin7(1'b0), .pin8(OUT[6]), .pin9(_74157_10_pin9), .pin10(NO), .pin11(OUT[7]), .pin12(_74157_10_pin12),
    .pin13(NO), .pin14(1'b1));
  _7486 _7486_11 (
    .pin1(_74157_11_pin4), .pin2(NO), .pin3(OUT[8]), .pin4(_74157_11_pin7), .pin5(NO), .pin6(OUT[9]),
    .pin7(1'b0), .pin8(OUT[10]), .pin9(_74157_11_pin9), .pin10(NO), .pin11(OUT[11]), .pin12(_74157_11_pin12),
    .pin13(NO), .pin14(1'b1));
  _7486 _7486_12 (
    .pin1(_74157_12_pin4), .pin2(NO), .pin3(OUT[12]), .pin4(_74157_12_pin7), .pin5(NO), .pin6(OUT[13]),
    .pin7(1'b0), .pin8(OUT[14]), .pin9(_74157_12_pin9), .pin10(NO), .pin11(NG), .pin12(_74157_12_pin12),
    .pin13(NO), .pin14(1'b1));
  _74688 _74688_1 (
    .pin1(1'b0), .pin2(OUT[0]), .pin3(1'b0), .pin4(OUT[1]), .pin5(1'b0), .pin6(OUT[2]), .pin7(1'b0),
    .pin8(OUT[3]), .pin9(1'b0), .pin10(1'b0), .pin11(OUT[4]), .pin12(1'b0), .pin13(OUT[5]), .pin14(1'b0),
    .pin15(OUT[6]), .pin16(1'b0), .pin17(OUT[7]), .pin18(1'b0), .pin19(_74688_1_pin19), .pin20(1'b1));
  _74688 _74688_2 (
    .pin1(1'b0), .pin2(OUT[8]), .pin3(1'b0), .pin4(OUT[9]), .pin5(1'b0), .pin6(OUT[10]), .pin7(1'b0),
    .pin8(OUT[11]), .pin9(1'b0), .pin10(1'b0), .pin11(OUT[12]), .pin12(1'b0), .pin13(OUT[13]), .pin14(1'b0),
    .pin15(OUT[14]), .pin16(1'b0), .pin17(NG), .pin18(1'b0), .pin19(_74688_2_pin19), .pin20(1'b1));
  _74245 _74245_1 (
    .pin1(1'b1), .pin2(NG), .pin3(ZR), .pin10(1'b0), .pin17(_74245_1_pin17), .pin18(_74245_1_pin18),
    .pin19(not_1_out), .pin20(1'b1));  // open: pin4, pin5, pin6, pin7, pin8, pin9, pin11, pin12, pin13, pin14, pin15, pin16
  _74245 _74245_2 (
    .pin1(1'b1), .pin2(OUT[0]), .pin3(OUT[1]), .pin4(OUT[2]), .pin5(OUT[3]), .pin6(OUT[4]), .pin7(OUT[5]),
    .pin8(OUT[6]), .pin9(OUT[7]), .pin10(1'b0), .pin11(_74245_2_pin11), .pin12(_74245_2_pin12),
    .pin13(_74245_2_pin13), .pin14(_74245_2_pin14), .pin15(_74245_2_pin15), .pin16(_74245_2_pin16),
    .pin17(_74245_2_pin17), .pin18(_74245_2_pin18), .pin19(not_1_out), .pin20(1'b1));
  _74245 _74245_3 (
    .pin1(1'b1), .pin2(OUT[8]), .pin3(OUT[9]), .pin4(OUT[10]), .pin5(OUT[11]), .pin6(OUT[12]),
    .pin7(OUT[13]), .pin8(OUT[14]), .pin9(NG), .pin10(1'b0), .pin11(_74245_3_pin11), .pin12(_74245_3_pin12),
    .pin13(_74245_3_pin13), .pin14(_74245_3_pin14), .pin15(_74245_3_pin15), .pin16(_74245_3_pin16),
    .pin17(_74245_3_pin17), .pin18(_74245_3_pin18), .pin19(not_1_out), .pin20(1'b1));
  LED led_1 (.in(_74245_3_pin12));
  LED led_2 (.in(_74245_3_pin11));
  LED u_NG (.in(_74245_1_pin18));
  LED led_3 (.in(_74245_3_pin14));
  LED led_4 (.in(_74245_3_pin13));
  LED u_ZR (.in(_74245_1_pin17));
  LED led_5 (.in(_74245_3_pin16));
  LED led_6 (.in(_74245_3_pin15));
  _7402 _7402_1 (
    .pin1(ZR), .pin2(_74688_1_pin19), .pin3(_74688_2_pin19), .pin5(1'b0), .pin6(1'b0), .pin7(1'b0),
    .pin8(1'b0), .pin9(1'b0), .pin11(1'b0), .pin12(1'b0), .pin14(1'b1));  // open: pin4, pin10, pin13
  LED led_7 (.in(_74245_3_pin18));
  LED led_8 (.in(_74245_3_pin17));
  LED led_9 (.in(_74245_2_pin12));
  LED led_10 (.in(_74245_2_pin11));
  LED led_11 (.in(_74245_2_pin14));
  LED led_12 (.in(_74245_2_pin13));
  LED led_13 (.in(_74245_2_pin16));
  LED led_14 (.in(_74245_2_pin15));
  LED led_15 (.in(_74245_2_pin18));
  LED led_16 (.in(_74245_2_pin17));

  assign OUT[15] = NG;
endmodule

/* Test case:
X  Y      ZX NX ZY NY F  NO OUT    ZR NG
0  65535  1  0  1  0  1  0  0      1  0
0  65535  1  1  1  1  1  1  1      0  0 
0  65535  1  1  1  0  1  0  65535  0  1 
0  65535  0  0  1  1  0  0  0      1  0 
0  65535  1  1  0  0  0  0  65535  0  1 
0  65535  0  0  1  1  0  1  65535  0  1 
0  65535  1  1  0  0  0  1  0      1  0 
0  65535  0  0  1  1  1  1  0      1  0 
0  65535  1  1  0  0  1  1  1      0  0 
0  65535  0  1  1  1  1  1  1      0  0 
0  65535  1  1  0  1  1  1  0      1  0 
0  65535  0  0  1  1  1  0  65535  0  1 
0  65535  1  1  0  0  1  0  65534  0  1 
0  65535  0  0  0  0  1  0  65535  0  1 
0  65535  0  1  0  0  1  1  1      0  0 
0  65535  0  0  0  1  1  1  65535  0  1 
0  65535  0  0  0  0  0  0  0      1  0 
0  65535  0  1  0  1  0  1  65535  0  1 
17 3      1  0  1  0  1  0  0      1  0 
17 3      1  1  1  1  1  1  1      0  0 
17 3      1  1  1  0  1  0  65535  0  1 
17 3      0  0  1  1  0  0  17     0  0 
17 3      1  1  0  0  0  0  3      0  0 
17 3      0  0  1  1  0  1  65518  0  1 
17 3      1  1  0  0  0  1  65532  0  1 
17 3      0  0  1  1  1  1  65519  0  1 
17 3      1  1  0  0  1  1  65533  0  1 
17 3      0  1  1  1  1  1  18     0  0 
17 3      1  1  0  1  1  1  4      0  0 
17 3      0  0  1  1  1  0  16     0  0 
17 3      1  1  0  0  1  0  2      0  0 
17 3      0  0  0  0  1  0  20     0  0 
17 3      0  1  0  0  1  1  14     0  0 
17 3      0  0  0  1  1  1  65522  0  1 
17 3      0  0  0  0  0  0  1      0  0 
17 3      0  1  0  1  0  1  19     0  0 
*/
