// Digital circuit CPU.dig as structural Verilog
module CPU (
  input  [15:0] Ins,
  input  [15:0] InM,
  input  Cl,
  input  Res,
  output WrM,
  output [15:0] AM,
  output [15:0] OM,
  output [15:0] PC,
  output [15:0] DO
);

  wire _7404_1_pin2, _7404_1_pin3, _7404_1_pin4, _7404_1_pin5, _7404_1_pin6, _7404_1_pin8, _7404_1_pin9,
       _7408_1_pin3, _7408_2_pin3, _7408_2_pin6, _7408_2_pin8, _7408_2_pin11, _7408_3_pin3, _7408_3_pin6,
       _7408_3_pin10, _7408_3_pin11, _7408_3_pin12, _7432_1_pin3, _74238_1_pin7, _74238_1_pin9,
       _74238_1_pin10, _74238_1_pin11, _74238_1_pin12, _74238_1_pin13, _74238_1_pin14;
  wire [15:0] _16bit_mux_1_out, _16bit_mux_2_out;

  _7408 _7408_1 (
    .pin1(Ins[15]), .pin2(Ins[4]), .pin3(_7408_1_pin3), .pin4(Ins[15]), .pin5(Ins[3]), .pin6(WrM),
    .pin7(1'b0), .pin9(1'b0), .pin10(1'b0), .pin12(1'b0), .pin13(1'b0), .pin14(1'b1));  // open: pin8, pin11
  _7404 _7404_1 (
    .pin1(Ins[15]), .pin2(_7404_1_pin2), .pin3(_7404_1_pin3), .pin4(_7404_1_pin4), .pin5(_7404_1_pin5),
    .pin6(_7404_1_pin6), .pin7(1'b0), .pin8(_7404_1_pin8), .pin9(_7404_1_pin9), .pin11(1'b0), .pin13(1'b0),
    .pin14(1'b1));  // open: pin10, pin12
  _74238 _74238_1 (
    .pin1(Ins[0]), .pin2(Ins[1]), .pin3(Ins[2]), .pin4(1'b0), .pin5(1'b0), .pin6(1'b1), .pin7(_74238_1_pin7),
    .pin8(1'b0), .pin9(_74238_1_pin9), .pin10(_74238_1_pin10), .pin11(_74238_1_pin11),
    .pin12(_74238_1_pin12), .pin13(_74238_1_pin13), .pin14(_74238_1_pin14), .pin16(1'b1));  // open: pin15
  _7408 _7408_2 (
    .pin1(_7404_1_pin4), .pin2(_7404_1_pin6), .pin3(_7408_2_pin3), .pin4(_7408_2_pin3),
    .pin5(_74238_1_pin14), .pin6(_7408_2_pin6), .pin7(1'b0), .pin8(_7408_2_pin8), .pin9(_7404_1_pin4),
    .pin10(_74238_1_pin12), .pin11(_7408_2_pin11), .pin12(_7404_1_pin5), .pin13(_74238_1_pin13), .pin14(1'b1));
  _16bit_mux _16bit_mux_1 (.A(Ins), .S(Ins[15]), .B(OM), .Out(_16bit_mux_1_out));
  _16bit_mux _16bit_mux_2 (.A(AM), .S(Ins[12]), .B(InM), .Out(_16bit_mux_2_out));
  _7408 _7408_3 (
    .pin1(_74238_1_pin11), .pin2(_7404_1_pin3), .pin3(_7408_3_pin3), .pin4(_74238_1_pin10),
    .pin5(_7404_1_pin6), .pin6(_7408_3_pin6), .pin7(1'b0), .pin8(_7404_1_pin9), .pin9(Ins[15]),
    .pin10(_7408_3_pin10), .pin11(_7408_3_pin11), .pin12(_7408_3_pin12), .pin13(_74238_1_pin9), .pin14(1'b1));
  _16bit_register D_Register (.D(OM), .L(_7408_1_pin3), .E(1'b1), .Cl(Cl), .ED(1'b0), .Out(DO));
  _7432 _7432_1 (
    .pin1(_7404_1_pin2), .pin2(Ins[5]), .pin3(_7432_1_pin3), .pin4(_7404_1_pin3), .pin5(_7404_1_pin5),
    .pin6(_7408_3_pin12), .pin7(1'b0), .pin9(1'b0), .pin10(1'b0), .pin12(1'b0), .pin13(1'b0), .pin14(1'b1));  // open: pin8, pin11
  _16bit_register A_Register (.D(_16bit_mux_1_out), .L(_7432_1_pin3), .E(1'b1), .Cl(Cl), .ED(1'b0), .Out(AM));
  _74688 _74688_1 (
    .pin1(1'b0), .pin2(1'b0), .pin3(1'b0), .pin4(_7408_2_pin6), .pin5(1'b0), .pin6(_7408_2_pin11),
    .pin7(1'b0), .pin8(_7408_2_pin8), .pin9(1'b0), .pin10(1'b0), .pin11(_7408_3_pin3), .pin12(1'b0),
    .pin13(_7408_3_pin6), .pin14(1'b0), .pin15(_7408_3_pin11), .pin16(1'b0), .pin17(_74238_1_pin7),
    .pin18(1'b0), .pin19(_7408_3_pin10), .pin20(1'b1));
  ALU alu_1 (
    .X(DO), .ZX(Ins[11]), .NX(Ins[10]), .NO(Ins[6]), .Y(_16bit_mux_2_out), .ZY(Ins[9]), .NY(Ins[8]),
    .F(Ins[7]), .ED(1'b0), .OUT(OM), .NG(_7404_1_pin3), .ZR(_7404_1_pin5));
  _16bit_program_counter _16bit_program_counter_1 (
    .EO(1'b1), .D(AM), .Inc(_7404_1_pin8), .Cl(Cl), .Clr(Res), .Load(_7404_1_pin9), .ED(1'b0), .Out(PC));
endmodule

/* Test case:
Ins   Cl InM   Res WrM PC  OM    AM    DO
12345 0  0     0   0   0   X     0     0
12345 1  0     0   0   1   X     12345 0
60432 0  0     0   0   1   X     12345 0
60432 1  0     0   0   2   X     12345 12345
23456 0  0     0   0   2   X     12345 12345
23456 1  0     0   0   3   X     23456 12345
57808 0  0     0   0   3   X     23456 12345
57808 1  0     0   0   4   X     23456 11111
1000  0  0     0   0   4   X     23456 11111
1000  1  0     0   0   5   X     1000  11111
58120 0  0     0   1   5   11111 1000  11111
58120 1  0     0   1   6   11111 1000  11111
1001  0  0     0   0   6   X     1000  11111
1001  1  0     0   0   7   X     1001  11111
58264 0  0     0   1   7   11110 1001  11111
58264 1  0     0   1   8   11109 1001  11110
1000  0  0     0   0   8   X     1001  11110
1000  1  0     0   0   9   X     1000  11110
62672 0  11111 0   0   9   X     1000  11110
62672 1  11111 0   0   10  X     1000  65535
14    0  11111 0   0   10  X     1000  65535
14    1  11111 0   0   11  X     14    65535
58116 0  11111 0   0   11  X     14    65535
58116 1  11111 0   0   14  X     14    65535
999   0  11111 0   0   14  X     14    65535
999   1  11111 0   0   15  X     999   65535
60896 0  11111 0   0   15  X     999   65535
60896 1  11111 0   0   16  X     1000  65535
58120 0  11111 0   1   16  65535 1000  65535
58120 1  11111 0   1   17  65535 1000  65535
21    0  11111 0   0   17  X     1000  65535
21    1  11111 0   0   18  X     21    65535
59330 0  11111 0   0   18  X     21    65535
59330 1  11111 0   0   21  X     21    65535
2     0  11111 0   0   21  X     21    65535
2     1  11111 0   0   22  X     2     65535
57488 0  11111 0   0   22  X     2     65535
57488 1  11111 0   0   23  X     2     1
1000  0  11111 0   0   23  X     2     1
1000  1  11111 0   0   24  X     1000  1
61072 0  11111 0   0   24  X     1000  1
61072 1  11111 0   0   25  X     1000  65535
58113 0  11111 0   0   25  X     1000  65535
58113 1  11111 0   0   26  X     1000  65535
58114 0  11111 0   0   26  X     1000  65535
58114 1  11111 0   0   27  X     1000  65535
58115 0  11111 0   0   27  X     1000  65535
58115 1  11111 0   0   28  X     1000  65535
58116 0  11111 0   0   28  X     1000  65535
58116 1  11111 0   0   1000 X    1000  65535
58117 0  11111 0   0   1000 X    1000  65535
58117 1  11111 0   0   1000 X    1000  65535
58118 0  11111 0   0   1000 X    1000  65535
58118 1  11111 0   0   1000 X    1000  65535
58119 0  11111 0   0   1000 X    1000  65535
58119 1  11111 0   0   1000 X    1000  65535
60048 0  11111 0   0   1000 X    1000  65535
60048 1  11111 0   0   1001 X    1000  0
58113 0  11111 0   0   1001 X    1000  0
58113 1  11111 0   0   1002 X    1000  0
58114 0  11111 0   0   1002 X    1000  0
58114 1  11111 0   0   1000 X    1000  0
58115 0  11111 0   0   1000 X    1000  0
58115 1  11111 0   0   1000 X    1000  0
58116 0  11111 0   0   1000 X    1000  0
58116 1  11111 0   0   1001 X    1000  0
58117 0  11111 0   0   1001 X    1000  0
58117 1  11111 0   0   1002 X    1000  0
58118 0  11111 0   0   1002 X    1000  0
58118 1  11111 0   0   1000 X    1000  0
58119 0  11111 0   0   1000 X    1000  0
58119 1  11111 0   0   1000 X    1000  0
61392 0  11111 0   0   1000 X    1000  0
61392 1  11111 0   0   1001 X    1000  1
58113 0  11111 0   0   1001 X    1000  1
58113 1  11111 0   0   1000 X    1000  1
58114 0  11111 0   0   1000 X    1000  1
58114 1  11111 0   0   1001 X    1000  1
58115 0  11111 0   0   1001 X    1000  1
58115 1  11111 0   0   1000 X    1000  1
58116 0  11111 0   0   1000 X    1000  1
58116 1  11111 0   0   1001 X    1000  1
58117 0  11111 0   0   1001 X    1000  1
58117 1  11111 0   0   1000 X    1000  1
58118 0  11111 0   0   1000 X    1000  1
58118 1  11111 0   0   1001 X    1000  1
58119 0  11111 0   0   1001 X    1000  1
58119 1  11111 0   0   1000 X    1000  1
58119 0  11111 1   0   0    X    1000  1
58119 1  11111 1   0   0    X    1000  1
32767 0  11111 0   0   0    X    1000  1
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*/
