// Digital circuit Computer.dig as structural Verilog
module Computer (
  input  Start,
  input  clk,
  input  Reset,
  input  Manual_Clock,
  output [15:0] D_out
);

  wire and_1_out, switchdt_1_p1, switchdt_1_p8;
  wire [15:0] switchdt_1_p4, switchdt_1_p5, switchdt_1_p10, switchdt_1_p11, switchdt_1_p12;

  and and_1 (and_1_out, Start, clk);
  // SwitchDT switchdt_1: pin names not known; wires that end beside it: switchdt_1_p1, and_1_out, Manual_Clock, switchdt_1_p4, switchdt_1_p5, switchdt_1_p1, Reset, switchdt_1_p8, D_out, switchdt_1_p10, switchdt_1_p11, switchdt_1_p12
  CPU cpu_1 ();
  EEPROM #(.AddrBits(16), .Bits(16)) eeprom_1 (.A(switchdt_1_p10), .CS(1'b1), .WE(1'b0), .OE(1'b1), .D(switchdt_1_p4));
  RAMDualPort #(.AddrBits(16), .Bits(16)) ramdualport_1 (
    .A(switchdt_1_p12), .Din(switchdt_1_p11), .str(switchdt_1_p8), .C(switchdt_1_p1), .ld(1'b1),
    .D(switchdt_1_p5));

  // Notes on the sheet:
  //   clk: Hz: 10
  //   contents of eeprom_1 (hex, n*v repeats v):
  //   100,ec10,0,e308,1,ec10,1,e308,0,fc10,1,f4d0,fdc8,fdc8,fdd0
endmodule
